# Fritzing sketch water sensors (saved by Fritzing 0.9.3b)
breadboards: 1

parts:
  S1 = PH meter [package=THT]
  S2 = PH meter [package=THT]
  Part1 = Arduino Uno (Rev3)

nets:
  N1: S1.pin1, Part1.A0
  N2: S1.pin2, S2.pin2, Part1.5V
  N3: S1.pin3, S2.pin3, Part1.GND
  N4: S2.pin1, Part1.A1
